# Fritzing sketch pc-audio-mixer (saved by Fritzing 1.0.6)
breadboards: 1

parts:
  ADC1 = MCP3008 [package=dil16]
  Mod1 = Raspberry Pi Pico
  C1 = Capacitor [mn=100nF package=cap-pth-small2]
  C2 = Capacitor [mn=100nF package=cap-pth-small2]
  C3 = Electrolytic Capacitor [capacitance=1µF voltage=35V package="100 mil [THT, electrolytic]"]
  R1 = Rotary Potentiometer (Large) [maximum_resistance=100kΩ knob_status=50% power=0.5W package=THT]
  R2 = Resistor [tolerance=±5% power=0.25W resistance=220 package=THT]
  C4 = Capacitor [package=cap-pth-small2]

nets:
  N1: ADC1.CH0, R2.Pin_0, C4.2
  N2: ADC1.DGND, ADC1.AGND, Mod1.pin_3, Mod1.pin_8, Mod1.pin_13, Mod1.pin_18, Mod1.pin_23, Mod1.pin_28, Mod1.pin_33, Mod1.pin_38, Mod1.pin_42, C3.-, C4.1
  N3: ADC1.CS/SHDN, Mod1.pin_22
  N4: ADC1.Din, Mod1.pin_25
  N5: ADC1.Dout, Mod1.pin_21
  N6: ADC1.CLK, Mod1.pin_24
  N7: ADC1.VREF, ADC1.VDD, Mod1.pin_36, C1.2, C2.2, C3.+
  N8: C1.1, C2.1
  N9: R1.wiper, R2.Pin_1

custom parts:
  Raspberry Pi Pico: Raspberry Pi Pico. Based around the RP2040 microcontroller the Pico is a low cost microcontroller device bringing Raspberry Pi quality, cost, and easy of use to the microcontroller space. Jan 2021, Split part in to two versions: tht (this one) and SMD. This one will drill holes for a .1 in header in pcb to allow plugging in the module as well as providing pads to solder the module to the top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
